# Fritzing sketch breadboard_using (saved by Fritzing 1.0.1rc)
breadboards: 1

parts:
  BAT1 = Battery Holders [package=battery-aa-kit]
  LED1 = LED - 3mm [color="Red (633nm)" current=0.030A package="3 mm [THT]"]
  U1 = SN74LS14N [package="DIP14 [THT]"]

nets:
  N1: BAT1.+, LED1.cathode, U1.VCC
  N2: BAT1.-, LED1.anode, U1.GND
